// Logisim project cpu.circ as structural Verilog: 2 circuits, main circuit main
module main (
  input  [31:0] INSTRUCTION,
  input  CLOCK,
  output [31:0] FETCH_ADDRESS,
  output [31:0] s0_Value,
  output [31:0] s1_Value,
  output [31:0] t0_Value,
  output [31:0] t1_Value,
  output [31:0] a0_Value,
  output [31:0] ra_Value,
  output [31:0] sp_Value
);

  wire ALUSel, ASel, BSel, MEM_p1, MEM_p3, MEM_p5, MEM_p10, MemRW, PCSel, RegWEn, undriven, WBSel;
  wire [24:0] demultiplexer_1_out1, Iimm, SBimm, Simm, Uimm, UJimm;
  wire [24:13] iImm_t;
  wire [31:0] adder_1_out, bit_extender_1_out, bit_extender_2_out, bit_extender_3_out, bit_extender_4_out,
       immGen, main_1_read_data_1, main_1_read_data_2, main_2_result, MEM_p11, multiplexer_1_out,
       multiplexer_3_out, multiplexer_4_out, multiplexer_5_out;

  Multiplexer #(.width(32)) multiplexer_1 (
    .in0(adder_1_out), .in1(main_2_result), .out(multiplexer_1_out), .sel(PCSel));  // open: en
  Register #(.width(32)) PC (.D(multiplexer_1_out), .Q(FETCH_ADDRESS), .clk(CLOCK));  // open: en, clr
  Adder #(.width(32)) adder_1 (.a(FETCH_ADDRESS), .b(32'h4), .out(adder_1_out));  // open: cin, cout
  assign bit_extender_1_out = {{20{1'b0}}, iImm_t};  // Bit_Extender bit_extender_1
  assign bit_extender_2_out = {{20{1'b0}}, {Simm[24:18], Simm[4:0]}};  // Bit_Extender bit_extender_2
  assign bit_extender_3_out = {{19{1'b0}}, {SBimm[24], SBimm[0], SBimm[23:18], SBimm[4:1], 1'b0}};  // Bit_Extender bit_extender_3
  assign bit_extender_4_out = {{11{1'b0}}, {UJimm[24], UJimm[12:5], UJimm[13], UJimm[23:14], 1'b0}};  // Bit_Extender bit_extender_4
  Demultiplexer #(.select(3), .width(25)) demultiplexer_1 (
    .out0(Iimm), .out1(demultiplexer_1_out1), .out2(SBimm), .out3(Uimm), .out4(UJimm), .in(INSTRUCTION[31:7]));  // open: out5, out6, out7, sel, en
  Multiplexer #(.select(3), .width(32)) multiplexer_2 (
    .in0(bit_extender_1_out), .in1(bit_extender_2_out), .in2(bit_extender_3_out),
    .in3({Uimm[24:5], {12{1'b0}}}), .in4(bit_extender_4_out), .out(immGen), .en(undriven));  // open: in5, in6, in7, sel
  regfile_main main_1 (
    .Read_Register_1__rs1(INSTRUCTION[19:15]), .Read_Register_2__rs2(INSTRUCTION[24:20]),
    .Write_Register__rd(INSTRUCTION[11:7]), .Write_Data(multiplexer_5_out), .Write_Enable(RegWEn),
    .Clock(CLOCK), .Read_Data_1(main_1_read_data_1), .Read_Data_2(main_1_read_data_2), .s1_Value(s1_Value),
    .t0_Value(t0_Value), .t1_Value(t1_Value), .a0_Value(a0_Value), .s0_Value(s0_Value), .ra_Value(ra_Value),
    .sp_Value(sp_Value));
  Multiplexer #(.width(32)) multiplexer_3 (
    .in0(main_1_read_data_2), .in1(immGen), .out(multiplexer_3_out), .sel(BSel));  // open: en
  Multiplexer #(.width(32)) multiplexer_4 (
    .in0(main_1_read_data_1), .in1(adder_1_out), .out(multiplexer_4_out), .sel(ASel));  // open: en
  alu_main main_2 (
    .Switch(4'b0010), .X(multiplexer_4_out), .Result(main_2_result), .Y(multiplexer_3_out));  // open: Equal
  // mem_main MEM: pin names not known; wires that end beside it: MEM_p1, ALUSel, MEM_p3, MEM_p3, MEM_p5, main_2_result, MemRW, MEM_p5, CLOCK, MEM_p10, MEM_p11, WBSel
  control_unit control_unit_1 ();  // open: in_1
  Multiplexer #(.select(2), .width(32)) multiplexer_5 (
    .in1(main_2_result), .in2(MEM_p11), .out(multiplexer_5_out), .sel(2'b01));  // open: in0, in3, en

  // Other names for the same wires on the sheet: a0[31:0] = a0_Value; clk = CLOCK; fetch_addr[31:0] = FETCH_ADDRESS;
  //   ra[31:0] = ra_Value; s0[31:0] = s0_Value; s1[31:0] = s1_Value; sp[31:0] = sp_Value; t0[31:0] = t0_Value;
  //   t1[31:0] = t1_Value

  // Notes on the sheet:
  //   Output
  //   These are outputs/inputs from run.circ
  //   Inputs
  //   These are DEBUG/TEST outputs from your circuit.
endmodule

module control_unit (
  input  [31:0] in_1
);

  Demultiplexer #(.select(5), .width(32)) demultiplexer_1 (
    .in(in_1), .sel(in_1[6:2]));  // open: out0, out1, out2, out3, out4, out5, out6, out7, out8, out9, out10, out11, out12, out13, out14, out15, out16, out17, out18, out19, out20, out21, out22, out23, out24, out25, out26, out27, out28, out29, out30, out31, en
  Demultiplexer #(.select(3), .width(32)) demultiplexer_2 ();  // open: out0, out1, out2, out3, out4, out5, out6, out7, in, sel, en
endmodule
